# Fritzing sketch RPiKeurig (saved by Fritzing 0.9.2b)
breadboards: 1

parts:
  Raspberry_Pi1 = Raspberry Pi (Model B)
  R1 = Resistor [tolerance=±5% resistance=220 package=THT]
  J1 = Basic Servo

nets:
  5V: Raspberry_Pi1.5V, J1.vcc
  GND: Raspberry_Pi1.GND, J1.gnd
  N1: Raspberry_Pi1.#23, R1.Pin_1
  N2: R1.Pin_0, J1.pulse

custom parts:
  Raspberry Pi (Model B): Raspberry Pi Single-board Computer, Model B
